// Logisim project Worder16.circ as structural Verilog: 2 circuits, main circuit main
module main (
);

  wire accs, adder_1_cout, albe, albs, and_1_out, and_2_out, and_3_out, and_4_out, and_5_out, clock_1_out,
       counter_1_q, decoder_1_out0, decoder_1_out1, decoder_1_out2, decoder_2_out0, decoder_2_out1,
       decoder_2_out2, decoder_3_out1, flags, iare, iars, mare, mars, mdrie, mdris, mdroe, mdros, mucs,
       not_1_out, not_2_out, or_1_out, or_2_out, or_3_out, pccount, pcenb, pcinc, pcset,
       pull_resistor_49_node, ramr, ramw, reg1e, reg1s, reg2e, reg2s, regse, regss, spcount, spenb, spinc,
       xor_1_out;
  wire [3:0] controlled_buffer_1_out, controlled_buffer_1_out_2, controlled_buffer_3_out,
       controlled_buffer_4_out, counter_2_q, counter_4_q, rdw_q, rdw_q_2, rdw_q_3, rdw_q_4, rew_q, rew_q_2,
       rew_q_3, rew_q_4, rfw_q, rfw_q_2, rfw_q_3, rfw_q_4, rgw_q, rgw_q_2, rgw_q_3, rgw_q_4, rhw_q, rhw_q_2,
       rhw_q_3, rhw_q_4, riw_q, riw_q_2, riw_q_3, riw_q_4, rjw_q, rjw_q_2, rjw_q_3, rjw_q_4, rkw_q, rkw_q_2,
       rkw_q_3, rkw_q_4, rlw_q, rlw_q_2, rlw_q_3, rlw_q_4, rmw_q, rmw_q_2, rmw_q_3, rmw_q_4, rnw_q, rnw_q_2,
       rnw_q_3, rnw_q_4, rpw_q, rpw_q_2, rpw_q_3, rpw_q_4, rqw_q, rqw_q_2, rqw_q_3, rqw_q_4;
  wire [4:0] customcomparator_1_carry, ledbar_1_p1;
  wire [9:9] or_4_out;
  wire [15:0] acc_q, adder_1_out, adder_2_out, alb_q, and_6_out, controlled_buffer_9_out,
       controlled_buffer_10_out, controlled_buffer_25_out, controlled_buffer_26_out,
       controlled_buffer_27_out, controlled_buffer_28_out, controlled_buffer_30_out, counter_3_q,
       decoder_3_out0, muc_q, multiplier_1_cout, multiplier_1_out, not_3_out, or_5_out, or_9_out,
       pull_resistor_41_node, ram_1_dout, register_1_q, register_3_q, register_4_q, register_5_q,
       register_6_q, shifter_1_out, shifter_2_out, shifter_3_out, shifter_4_out, subtractor_1_out,
       subtractor_2_out, xor_2_out;
  wire [15:4] undriven;
  wire [15:8] controlled_buffer_1_out_3;

  Register #(.trigger("high"), .width(16)) register_1 (
    .D(controlled_buffer_9_out), .en(decoder_1_out2), .clk(xor_1_out), .Q(register_1_q));  // open: clr
  Counter #(.max('h1), .trigger("falling"), .width(1)) counter_1 (
    .clr(1'b0), .load(1'b0), .up(1'b1), .count(1'b1), .clk(clock_1_out), .D(1'b0), .Q(counter_1_q));  // open: carry
  Clock clock_1 (.out(clock_1_out));
  Counter #(.max('hf), .trigger("falling"), .width(4)) counter_2 (
    .clr(1'b0), .load(1'b0), .up(1'b1), .count(1'b1), .clk(counter_1_q), .D(4'b0000), .Q(counter_2_q));  // open: carry
  Decoder #(.enable("false"), .select(4)) decoder_1 (
    .out0(decoder_1_out0), .out1(decoder_1_out1), .out2(decoder_1_out2), .sel(counter_2_q));  // open: out3, out4, out5, out6, out7, out8, out9, out10, out11, out12, out13, out14, out15
  or or_1 (or_1_out, decoder_1_out0, decoder_1_out1, decoder_1_out2);
  or or_2 (or_2_out, regss, reg1s, reg2s);
  or or_3 (or_3_out, regse, reg1e, reg2e);
  Decoder #(.select(4)) decoder_2 (
    .out0(decoder_2_out0), .out1(decoder_2_out1), .out2(decoder_2_out2), .out3(or_5_out[3]),
    .out4(or_5_out[4]), .out5(or_5_out[5]), .out6(or_5_out[6]), .out7(or_5_out[7]), .out8(or_5_out[8]),
    .out9(or_5_out[9]), .out10(or_5_out[10]), .out11(or_5_out[11]), .out12(or_5_out[12]),
    .out13(or_5_out[13]), .out14(or_5_out[14]), .out15(or_5_out[15]), .sel(controlled_buffer_3_out),
    .en(or_2_out));
  Decoder #(.select(4)) decoder_3 (
    .out0(decoder_3_out0[0]), .out1(decoder_3_out1), .out2(decoder_3_out0[2]), .out3(decoder_3_out0[3]),
    .out4(decoder_3_out0[4]), .out5(decoder_3_out0[5]), .out6(decoder_3_out0[6]), .out7(decoder_3_out0[7]),
    .out8(decoder_3_out0[8]), .out9(decoder_3_out0[9]), .out10(decoder_3_out0[10]),
    .out11(decoder_3_out0[11]), .out12(decoder_3_out0[12]), .out13(decoder_3_out0[13]),
    .out14(decoder_3_out0[14]), .out15(decoder_3_out0[15]), .sel(controlled_buffer_4_out), .en(or_3_out));
  assign {controlled_buffer_1_out_3, controlled_buffer_1_out_2, controlled_buffer_1_out} = not_2_out ? register_1_q : 16'bz;  // Controlled_Buffer controlled_buffer_1
  not not_1 (not_1_out, not_2_out);
  assign {controlled_buffer_1_out_3, controlled_buffer_1_out_2, controlled_buffer_1_out} = not_1_out ? {16{1'b0}} : 16'bz;  // Controlled_Buffer controlled_buffer_2
  not not_2 (not_2_out, or_1_out);
  and and_1 (and_1_out, controlled_buffer_1_out_2[0], ledbar_1_p1[4]);
  assign controlled_buffer_3_out = regss ? controlled_buffer_1_out_2 : 4'bz;  // Controlled_Buffer controlled_buffer_3
  assign controlled_buffer_4_out = regse ? controlled_buffer_1_out_2 : 4'bz;  // Controlled_Buffer controlled_buffer_4
  assign controlled_buffer_3_out = reg1s ? controlled_buffer_1_out_2 : 4'bz;  // Controlled_Buffer controlled_buffer_5
  assign controlled_buffer_4_out = reg1e ? controlled_buffer_1_out_2 : 4'bz;  // Controlled_Buffer controlled_buffer_6
  assign controlled_buffer_3_out = reg2s ? controlled_buffer_1_out : 4'bz;  // Controlled_Buffer controlled_buffer_7
  assign controlled_buffer_4_out = reg2e ? controlled_buffer_1_out : 4'bz;  // Controlled_Buffer controlled_buffer_8
  xor xor_1 (xor_1_out, counter_1_q, 1'b0);
  and and_2 (and_2_out, controlled_buffer_1_out[3], ledbar_1_p1[3]);
  and and_3 (and_3_out, controlled_buffer_1_out[2], ledbar_1_p1[2]);
  and and_4 (and_4_out, controlled_buffer_1_out[1], ledbar_1_p1[1]);
  or or_4 (or_4_out[9], and_1_out, and_2_out, and_3_out, and_4_out, and_5_out);
  and and_5 (and_5_out, controlled_buffer_1_out[0], ledbar_1_p1[0]);
  ROM #(.addrWidth(10)) MemoryControlROM (
    .addr({or_4_out[9], controlled_buffer_1_out_3[15:11], counter_2_q}),
    .data({mdroe, mdros, mdrie, mdris, mare, mars, ramw, ramr}));
  ROM #(.addrWidth(10), .dataWidth(10)) CounterControlROM (
    .addr({or_4_out[9], controlled_buffer_1_out_3[15:11], counter_2_q}),
    .data({iare, iars, flags, spenb, spinc, spcount, pcenb, pcset, pcinc, pccount}));
  ROM #(.addrWidth(10), .dataWidth(10)) RegisterControlROM (
    .addr({or_4_out[9], controlled_buffer_1_out_3[15:11], counter_2_q}),
    .data({mucs, accs, albe, albs, reg2e, reg2s, reg1e, reg1s, regse, regss}));
  or or_5 (or_5_out[0], accs, decoder_2_out0);
  or or_6 (or_5_out[1], albs, decoder_2_out1);
  or or_7 (decoder_3_out0[1], albe, decoder_3_out1);
  or or_8 (or_5_out[2], mucs, decoder_2_out2);
  Register #(.trigger("high"), .width(16)) acc (
    .D(pull_resistor_41_node), .en(or_5_out[15]), .clk(xor_1_out), .Q(acc_q));  // open: clr
  Register #(.trigger("high"), .width(16)) alb (
    .D(controlled_buffer_9_out), .en(or_5_out[14]), .clk(xor_1_out), .Q(alb_q));  // open: clr
  Register #(.trigger("high"), .width(16)) muc (
    .D(multiplier_1_out), .en(or_5_out[13]), .clk(xor_1_out), .Q(muc_q));  // open: clr
  Register #(.trigger("high"), .width(16)) rdw (
    .D(controlled_buffer_9_out), .en(or_5_out[12]), .clk(xor_1_out), .Q({rdw_q_4, rdw_q_3, rdw_q_2, rdw_q}));  // open: clr
  Register #(.trigger("high"), .width(16)) rew (
    .D(controlled_buffer_9_out), .en(or_5_out[11]), .clk(xor_1_out), .Q({rew_q_4, rew_q_3, rew_q_2, rew_q}));  // open: clr
  Register #(.trigger("high"), .width(16)) rfw (
    .D(controlled_buffer_9_out), .en(or_5_out[10]), .clk(xor_1_out), .Q({rfw_q_4, rfw_q_3, rfw_q_2, rfw_q}));  // open: clr
  Register #(.trigger("high"), .width(16)) rgw (
    .D(controlled_buffer_9_out), .en(or_5_out[9]), .clk(xor_1_out), .Q({rgw_q_4, rgw_q_3, rgw_q_2, rgw_q}));  // open: clr
  Register #(.trigger("high"), .width(16)) rhw (
    .D(controlled_buffer_9_out), .en(or_5_out[8]), .clk(xor_1_out), .Q({rhw_q_4, rhw_q_3, rhw_q_2, rhw_q}));  // open: clr
  Register #(.trigger("high"), .width(16)) riw (
    .D(controlled_buffer_9_out), .en(or_5_out[7]), .clk(xor_1_out), .Q({riw_q_4, riw_q_3, riw_q_2, riw_q}));  // open: clr
  Register #(.trigger("high"), .width(16)) rjw (
    .D(controlled_buffer_9_out), .en(or_5_out[6]), .clk(xor_1_out), .Q({rjw_q_4, rjw_q_3, rjw_q_2, rjw_q}));  // open: clr
  Register #(.trigger("high"), .width(16)) rkw (
    .D(controlled_buffer_9_out), .en(or_5_out[5]), .clk(xor_1_out), .Q({rkw_q_4, rkw_q_3, rkw_q_2, rkw_q}));  // open: clr
  Register #(.trigger("high"), .width(16)) rlw (
    .D(controlled_buffer_9_out), .en(or_5_out[4]), .clk(xor_1_out), .Q({rlw_q_4, rlw_q_3, rlw_q_2, rlw_q}));  // open: clr
  Register #(.trigger("high"), .width(16)) rmw (
    .D(controlled_buffer_9_out), .en(or_5_out[3]), .clk(xor_1_out), .Q({rmw_q_4, rmw_q_3, rmw_q_2, rmw_q}));  // open: clr
  Register #(.trigger("high"), .width(16)) rnw (
    .D(controlled_buffer_9_out), .en(or_5_out[2]), .clk(xor_1_out), .Q({rnw_q_4, rnw_q_3, rnw_q_2, rnw_q}));  // open: clr
  Register #(.trigger("high"), .width(16)) rpw (
    .D(controlled_buffer_9_out), .en(or_5_out[1]), .clk(xor_1_out), .Q({rpw_q_4, rpw_q_3, rpw_q_2, rpw_q}));  // open: clr
  Register #(.trigger("high"), .width(16)) rqw (
    .D(controlled_buffer_9_out), .en(or_5_out[0]), .clk(xor_1_out), .Q({rqw_q_4, rqw_q_3, rqw_q_2, rqw_q}));  // open: clr
  assign controlled_buffer_9_out = decoder_3_out0[15] ? acc_q : 16'bz;  // Controlled_Buffer controlled_buffer_9
  assign controlled_buffer_10_out = decoder_3_out0[14] ? alb_q : 16'bz;  // Controlled_Buffer controlled_buffer_10
  assign controlled_buffer_9_out = decoder_3_out0[13] ? muc_q : 16'bz;  // Controlled_Buffer controlled_buffer_11
  assign controlled_buffer_9_out = decoder_3_out0[12] ? {rdw_q_4, rdw_q_3, rdw_q_2, rdw_q} : 16'bz;  // Controlled_Buffer controlled_buffer_12
  assign controlled_buffer_9_out = decoder_3_out0[11] ? {rew_q_4, rew_q_3, rew_q_2, rew_q} : 16'bz;  // Controlled_Buffer controlled_buffer_13
  assign controlled_buffer_9_out = decoder_3_out0[10] ? {rfw_q_4, rfw_q_3, rfw_q_2, rfw_q} : 16'bz;  // Controlled_Buffer controlled_buffer_14
  assign controlled_buffer_9_out = decoder_3_out0[9] ? {rgw_q_4, rgw_q_3, rgw_q_2, rgw_q} : 16'bz;  // Controlled_Buffer controlled_buffer_15
  assign controlled_buffer_9_out = decoder_3_out0[8] ? {rhw_q_4, rhw_q_3, rhw_q_2, rhw_q} : 16'bz;  // Controlled_Buffer controlled_buffer_16
  assign controlled_buffer_9_out = decoder_3_out0[7] ? {riw_q_4, riw_q_3, riw_q_2, riw_q} : 16'bz;  // Controlled_Buffer controlled_buffer_17
  assign controlled_buffer_9_out = decoder_3_out0[6] ? {rjw_q_4, rjw_q_3, rjw_q_2, rjw_q} : 16'bz;  // Controlled_Buffer controlled_buffer_18
  assign controlled_buffer_9_out = decoder_3_out0[5] ? {rkw_q_4, rkw_q_3, rkw_q_2, rkw_q} : 16'bz;  // Controlled_Buffer controlled_buffer_19
  assign controlled_buffer_9_out = decoder_3_out0[4] ? {rlw_q_4, rlw_q_3, rlw_q_2, rlw_q} : 16'bz;  // Controlled_Buffer controlled_buffer_20
  assign controlled_buffer_9_out = decoder_3_out0[3] ? {rmw_q_4, rmw_q_3, rmw_q_2, rmw_q} : 16'bz;  // Controlled_Buffer controlled_buffer_21
  assign controlled_buffer_9_out = decoder_3_out0[2] ? {rnw_q_4, rnw_q_3, rnw_q_2, rnw_q} : 16'bz;  // Controlled_Buffer controlled_buffer_22
  assign controlled_buffer_9_out = decoder_3_out0[1] ? {rpw_q_4, rpw_q_3, rpw_q_2, rpw_q} : 16'bz;  // Controlled_Buffer controlled_buffer_23
  assign controlled_buffer_9_out = decoder_3_out0[0] ? {rqw_q_4, rqw_q_3, rqw_q_2, rqw_q} : 16'bz;  // Controlled_Buffer controlled_buffer_24
  Pull_Resistor pull_resistor_1 (.node(controlled_buffer_9_out[15]));
  Pull_Resistor pull_resistor_2 (.node(pull_resistor_41_node[15]));
  Pull_Resistor pull_resistor_3 (.node(controlled_buffer_10_out[15]));
  Pull_Resistor pull_resistor_4 (.node(controlled_buffer_9_out[14]));
  Pull_Resistor pull_resistor_5 (.node(controlled_buffer_9_out[13]));
  Pull_Resistor pull_resistor_6 (.node(controlled_buffer_9_out[12]));
  Pull_Resistor pull_resistor_7 (.node(controlled_buffer_9_out[11]));
  Pull_Resistor pull_resistor_8 (.node(controlled_buffer_9_out[10]));
  Pull_Resistor pull_resistor_9 (.node(controlled_buffer_9_out[9]));
  Pull_Resistor pull_resistor_10 (.node(controlled_buffer_9_out[8]));
  Pull_Resistor pull_resistor_11 (.node(controlled_buffer_9_out[7]));
  Pull_Resistor pull_resistor_12 (.node(pull_resistor_41_node[14]));
  Pull_Resistor pull_resistor_13 (.node(pull_resistor_41_node[13]));
  Pull_Resistor pull_resistor_14 (.node(pull_resistor_41_node[12]));
  Pull_Resistor pull_resistor_15 (.node(pull_resistor_41_node[11]));
  Pull_Resistor pull_resistor_16 (.node(pull_resistor_41_node[10]));
  Pull_Resistor pull_resistor_17 (.node(pull_resistor_41_node[9]));
  Pull_Resistor pull_resistor_18 (.node(pull_resistor_41_node[8]));
  Pull_Resistor pull_resistor_19 (.node(pull_resistor_41_node[7]));
  Pull_Resistor pull_resistor_20 (.node(controlled_buffer_10_out[14]));
  Pull_Resistor pull_resistor_21 (.node(controlled_buffer_10_out[13]));
  Pull_Resistor pull_resistor_22 (.node(controlled_buffer_10_out[12]));
  Pull_Resistor pull_resistor_23 (.node(controlled_buffer_10_out[11]));
  Pull_Resistor pull_resistor_24 (.node(controlled_buffer_10_out[10]));
  Pull_Resistor pull_resistor_25 (.node(controlled_buffer_10_out[9]));
  Pull_Resistor pull_resistor_26 (.node(controlled_buffer_10_out[8]));
  Pull_Resistor pull_resistor_27 (.node(controlled_buffer_10_out[7]));
  Hex_Digit_Display #(.decimalPoint("false")) hex_digit_display_1 (.value(rdw_q_4));
  Hex_Digit_Display #(.decimalPoint("false")) hex_digit_display_2 (.value(rdw_q_3));
  Hex_Digit_Display #(.decimalPoint("false")) hex_digit_display_3 (.value(rew_q_4));
  Hex_Digit_Display #(.decimalPoint("false")) hex_digit_display_4 (.value(rew_q_3));
  Hex_Digit_Display #(.decimalPoint("false")) hex_digit_display_5 (.value(rfw_q_4));
  Hex_Digit_Display #(.decimalPoint("false")) hex_digit_display_6 (.value(rfw_q_3));
  Hex_Digit_Display #(.decimalPoint("false")) hex_digit_display_7 (.value(rgw_q_4));
  Hex_Digit_Display #(.decimalPoint("false")) hex_digit_display_8 (.value(rgw_q_3));
  Hex_Digit_Display #(.decimalPoint("false")) hex_digit_display_9 (.value(rhw_q_4));
  Hex_Digit_Display #(.decimalPoint("false")) hex_digit_display_10 (.value(rhw_q_3));
  Hex_Digit_Display #(.decimalPoint("false")) hex_digit_display_11 (.value(riw_q_4));
  Hex_Digit_Display #(.decimalPoint("false")) hex_digit_display_12 (.value(riw_q_3));
  Hex_Digit_Display #(.decimalPoint("false")) hex_digit_display_13 (.value(rjw_q_4));
  Hex_Digit_Display #(.decimalPoint("false")) hex_digit_display_14 (.value(rjw_q_3));
  Hex_Digit_Display #(.decimalPoint("false")) hex_digit_display_15 (.value(rkw_q_4));
  Hex_Digit_Display #(.decimalPoint("false")) hex_digit_display_16 (.value(rkw_q_3));
  Hex_Digit_Display #(.decimalPoint("false")) hex_digit_display_17 (.value(rlw_q_4));
  Hex_Digit_Display #(.decimalPoint("false")) hex_digit_display_18 (.value(rlw_q_3));
  Hex_Digit_Display #(.decimalPoint("false")) hex_digit_display_19 (.value(rmw_q_4));
  Hex_Digit_Display #(.decimalPoint("false")) hex_digit_display_20 (.value(rmw_q_3));
  Hex_Digit_Display #(.decimalPoint("false")) hex_digit_display_21 (.value(rnw_q_4));
  Hex_Digit_Display #(.decimalPoint("false")) hex_digit_display_22 (.value(rnw_q_3));
  Hex_Digit_Display #(.decimalPoint("false")) hex_digit_display_23 (.value(rpw_q_4));
  Hex_Digit_Display #(.decimalPoint("false")) hex_digit_display_24 (.value(rpw_q_3));
  Hex_Digit_Display #(.decimalPoint("false")) hex_digit_display_25 (.value(rqw_q_4));
  Hex_Digit_Display #(.decimalPoint("false")) hex_digit_display_26 (.value(rqw_q_3));
  Pull_Resistor pull_resistor_28 (.node(controlled_buffer_9_out[6]));
  Pull_Resistor pull_resistor_29 (.node(controlled_buffer_9_out[5]));
  Pull_Resistor pull_resistor_30 (.node(controlled_buffer_9_out[4]));
  Pull_Resistor pull_resistor_31 (.node(controlled_buffer_9_out[3]));
  Pull_Resistor pull_resistor_32 (.node(controlled_buffer_9_out[2]));
  Pull_Resistor pull_resistor_33 (.node(controlled_buffer_9_out[1]));
  Pull_Resistor pull_resistor_34 (.node(controlled_buffer_9_out[0]));
  // LedBar #(.inputtype("row"), .matrixcols(5)) ledbar_1: pin names not known; wires that end beside it: ledbar_1_p1
  Pull_Resistor pull_resistor_35 (.node(pull_resistor_41_node[6]));
  Pull_Resistor pull_resistor_36 (.node(pull_resistor_41_node[5]));
  Pull_Resistor pull_resistor_37 (.node(pull_resistor_41_node[4]));
  Pull_Resistor pull_resistor_38 (.node(pull_resistor_41_node[3]));
  Pull_Resistor pull_resistor_39 (.node(pull_resistor_41_node[2]));
  Pull_Resistor pull_resistor_40 (.node(pull_resistor_41_node[1]));
  Pull_Resistor pull_resistor_41 (.node(pull_resistor_41_node[0]));
  Pull_Resistor pull_resistor_42 (.node(controlled_buffer_10_out[6]));
  Pull_Resistor pull_resistor_43 (.node(controlled_buffer_10_out[5]));
  Pull_Resistor pull_resistor_44 (.node(controlled_buffer_10_out[4]));
  Pull_Resistor pull_resistor_45 (.node(controlled_buffer_10_out[3]));
  Pull_Resistor pull_resistor_46 (.node(controlled_buffer_10_out[2]));
  Pull_Resistor pull_resistor_47 (.node(controlled_buffer_10_out[1]));
  Pull_Resistor pull_resistor_48 (.node(controlled_buffer_10_out[0]));
  Hex_Digit_Display #(.decimalPoint("false")) hex_digit_display_27 (.value(rdw_q_2));
  Hex_Digit_Display #(.decimalPoint("false")) hex_digit_display_28 (.value(rdw_q));
  Hex_Digit_Display #(.decimalPoint("false")) hex_digit_display_29 (.value(rew_q_2));
  Hex_Digit_Display #(.decimalPoint("false")) hex_digit_display_30 (.value(rew_q));
  Hex_Digit_Display #(.decimalPoint("false")) hex_digit_display_31 (.value(rfw_q_2));
  Hex_Digit_Display #(.decimalPoint("false")) hex_digit_display_32 (.value(rfw_q));
  Hex_Digit_Display #(.decimalPoint("false")) hex_digit_display_33 (.value(rgw_q_2));
  Hex_Digit_Display #(.decimalPoint("false")) hex_digit_display_34 (.value(rgw_q));
  Hex_Digit_Display #(.decimalPoint("false")) hex_digit_display_35 (.value(rhw_q_2));
  Hex_Digit_Display #(.decimalPoint("false")) hex_digit_display_36 (.value(rhw_q));
  Hex_Digit_Display #(.decimalPoint("false")) hex_digit_display_37 (.value(riw_q_2));
  Hex_Digit_Display #(.decimalPoint("false")) hex_digit_display_38 (.value(riw_q));
  Hex_Digit_Display #(.decimalPoint("false")) hex_digit_display_39 (.value(rjw_q_2));
  Hex_Digit_Display #(.decimalPoint("false")) hex_digit_display_40 (.value(rjw_q));
  Hex_Digit_Display #(.decimalPoint("false")) hex_digit_display_41 (.value(rkw_q_2));
  Hex_Digit_Display #(.decimalPoint("false")) hex_digit_display_42 (.value(rkw_q));
  Hex_Digit_Display #(.decimalPoint("false")) hex_digit_display_43 (.value(rlw_q_2));
  Hex_Digit_Display #(.decimalPoint("false")) hex_digit_display_44 (.value(rlw_q));
  Hex_Digit_Display #(.decimalPoint("false")) hex_digit_display_45 (.value(rmw_q_2));
  Hex_Digit_Display #(.decimalPoint("false")) hex_digit_display_46 (.value(rmw_q));
  Hex_Digit_Display #(.decimalPoint("false")) hex_digit_display_47 (.value(rnw_q_2));
  Hex_Digit_Display #(.decimalPoint("false")) hex_digit_display_48 (.value(rnw_q));
  Hex_Digit_Display #(.decimalPoint("false")) hex_digit_display_49 (.value(rpw_q_2));
  Hex_Digit_Display #(.decimalPoint("false")) hex_digit_display_50 (.value(rpw_q));
  Hex_Digit_Display #(.decimalPoint("false")) hex_digit_display_51 (.value(rqw_q_2));
  Hex_Digit_Display #(.decimalPoint("false")) hex_digit_display_52 (.value(rqw_q));
  Register #(.trigger("high"), .width(5)) register_2 (
    .D(customcomparator_1_carry), .en(iare), .clk(iare), .Q(ledbar_1_p1));  // open: clr
  Register #(.trigger("high"), .width(16)) register_3 (
    .D(controlled_buffer_9_out), .en(flags), .clk(flags), .Q(register_3_q));  // open: clr
  Adder #(.width(16)) adder_1 (
    .a(controlled_buffer_9_out), .b(controlled_buffer_10_out), .out(adder_1_out),
    .cin(pull_resistor_49_node), .cout(adder_1_cout));
  Pull_Resistor pull_resistor_49 (.node(pull_resistor_49_node));
  Subtractor #(.width(16)) subtractor_1 (
    .a(controlled_buffer_9_out), .b(controlled_buffer_10_out), .out(subtractor_1_out),
    .bin(pull_resistor_49_node), .bout(adder_1_cout));
  Multiplier #(.width(16)) multiplier_1 (
    .a(controlled_buffer_9_out), .b(controlled_buffer_10_out), .out(multiplier_1_out),
    .cout(multiplier_1_cout));  // open: cin
  customcomparator customcomparator_1 (
    .Input_A(controlled_buffer_9_out), .Input_B(controlled_buffer_10_out), .CarryBorrow(adder_1_cout),
    .Carry(customcomparator_1_carry[0]), .A_Lgr(customcomparator_1_carry[1]),
    .Equal(customcomparator_1_carry[2]), .A_Zro(customcomparator_1_carry[3]),
    .A_Neg(customcomparator_1_carry[4]));
  assign and_6_out = controlled_buffer_9_out & controlled_buffer_10_out;  // AND_Gate and_6, 16 bits wide
  assign or_9_out = controlled_buffer_9_out | controlled_buffer_10_out;  // OR_Gate or_9, 16 bits wide
  assign xor_2_out = controlled_buffer_9_out ^ controlled_buffer_10_out;  // XOR_Gate xor_2, 16 bits wide
  assign not_3_out = ~controlled_buffer_9_out;  // NOT_Gate not_3, 16 bits wide
  Shifter #(.width(16)) shifter_1 (
    .in(controlled_buffer_9_out), .\dist (controlled_buffer_10_out[3:0]), .out(shifter_1_out));
  Shifter #(.shift("lr"), .width(16)) shifter_2 (
    .in(controlled_buffer_9_out), .\dist (controlled_buffer_10_out[3:0]), .out(shifter_2_out));
  Shifter #(.shift("rl"), .width(16)) shifter_3 (
    .in(controlled_buffer_9_out), .\dist (controlled_buffer_10_out[3:0]), .out(shifter_3_out));
  Shifter #(.shift("rr"), .width(16)) shifter_4 (
    .in(controlled_buffer_9_out), .\dist (controlled_buffer_10_out[3:0]), .out(shifter_4_out));
  Adder #(.width(16)) adder_2 (
    .a(controlled_buffer_9_out), .b({16{1'b0}}), .out(adder_2_out), .cin(1'b1));  // open: cout
  Subtractor #(.width(16)) subtractor_2 (
    .a(controlled_buffer_9_out), .b({16{1'b0}}), .out(subtractor_2_out), .bin(1'b1));  // open: bout
  assign controlled_buffer_25_out = iars ? register_3_q : 16'bz;  // Controlled_Buffer controlled_buffer_25
  Register #(.trigger("high"), .width(16)) register_4 (
    .D(controlled_buffer_25_out), .en(mars), .clk(mars), .Q(register_4_q));  // open: clr
  Register #(.trigger("high"), .width(16)) register_5 (
    .D(controlled_buffer_9_out), .en(mdris), .clk(mdris), .Q(register_5_q));  // open: clr
  Counter #(.max('hffff), .width(16)) counter_3 (
    .load(pcset), .up(pcinc), .count(pccount), .clk(counter_1_q), .D(controlled_buffer_26_out),
    .Q(counter_3_q));  // open: clr, carry
  assign controlled_buffer_26_out = pcset ? controlled_buffer_25_out : 16'bz;  // Controlled_Buffer controlled_buffer_26
  assign controlled_buffer_27_out = mare ? register_4_q : 16'bz;  // Controlled_Buffer controlled_buffer_27
  RAM #(.addrWidth(16), .dataWidth(16), .trigger("high")) ram_1 (
    .addr(controlled_buffer_27_out), .we(ramw), .oe(ramr), .din(controlled_buffer_28_out), .dout(ram_1_dout));
  assign controlled_buffer_28_out = mdrie ? register_5_q : 16'bz;  // Controlled_Buffer controlled_buffer_28
  Multiplexer #(.select(4), .width(16)) multiplexer_1 (
    .in0(adder_1_out), .in1(subtractor_1_out), .in2(multiplier_1_cout), .in4(and_6_out), .in5(or_9_out),
    .in6(xor_2_out), .in7(not_3_out), .in8(shifter_1_out), .in9(shifter_2_out), .in10(shifter_3_out),
    .in11(shifter_4_out), .in12(adder_2_out), .in13(subtractor_2_out), .out(pull_resistor_41_node));  // open: in3, in14, in15, sel
  Hex_Digit_Display #(.decimalPoint("false")) hex_digit_display_53 (.value(controlled_buffer_9_out[15:12]));
  Hex_Digit_Display #(.decimalPoint("false")) hex_digit_display_54 (.value(controlled_buffer_9_out[11:8]));
  Hex_Digit_Display #(.decimalPoint("false")) hex_digit_display_55 (.value(controlled_buffer_10_out[15:12]));
  Hex_Digit_Display #(.decimalPoint("false")) hex_digit_display_56 (.value(controlled_buffer_10_out[11:8]));
  Hex_Digit_Display #(.decimalPoint("false")) hex_digit_display_57 (.value(pull_resistor_41_node[15:12]));
  Hex_Digit_Display #(.decimalPoint("false")) hex_digit_display_58 (.value(pull_resistor_41_node[11:8]));
  assign controlled_buffer_25_out = pcenb ? counter_3_q : 16'bz;  // Controlled_Buffer controlled_buffer_29
  Hex_Digit_Display #(.decimalPoint("false")) hex_digit_display_59 (.value(controlled_buffer_9_out[7:4]));
  Hex_Digit_Display #(.decimalPoint("false")) hex_digit_display_60 (.value(controlled_buffer_9_out[3:0]));
  Hex_Digit_Display #(.decimalPoint("false")) hex_digit_display_61 (.value(controlled_buffer_10_out[7:4]));
  Hex_Digit_Display #(.decimalPoint("false")) hex_digit_display_62 (.value(controlled_buffer_10_out[3:0]));
  Hex_Digit_Display #(.decimalPoint("false")) hex_digit_display_63 (.value(pull_resistor_41_node[7:4]));
  Hex_Digit_Display #(.decimalPoint("false")) hex_digit_display_64 (.value(pull_resistor_41_node[3:0]));
  Counter #(.max('hf), .width(4)) counter_4 (
    .clr(1'b0), .load(1'b0), .up(spinc), .count(spcount), .clk(counter_1_q), .Q(counter_4_q));  // open: D, carry
  Register #(.trigger("high"), .width(16)) register_6 (
    .D(controlled_buffer_30_out), .en(mdros), .clk(mdros), .Q(register_6_q));  // open: clr
  assign controlled_buffer_30_out = ramr ? ram_1_dout : 16'bz;  // Controlled_Buffer controlled_buffer_30
  assign controlled_buffer_9_out = mdroe ? register_6_q : 16'bz;  // Controlled_Buffer controlled_buffer_31
  assign controlled_buffer_25_out = spenb ? {undriven, counter_4_q} : 16'bz;  // Controlled_Buffer controlled_buffer_32
  Pull_Resistor #(.pull(1)) pull_resistor_50 (.node(undriven[5]));
  Pull_Resistor #(.pull(1)) pull_resistor_51 (.node(undriven[7]));
endmodule

module customcomparator (
  input  CarryBorrow,
  input  [15:0] Input_A,
  input  [15:0] Input_B,
  output Carry,
  output A_Lgr,
  output Equal,
  output A_Zro,
  output A_Neg
);

  wire or_1_out;

  Comparator #(.mode("unsigned"), .width(16)) comparator_1 (
    .a(Input_A), .b(Input_B), .gt(A_Lgr), .eq(Equal));  // open: lt
  Comparator #(.mode("unsigned"), .width(16)) comparator_2 (.a(Input_A), .b({16{1'b0}}), .lt(A_Neg));  // open: gt, eq
  not not_1 (A_Zro, or_1_out);
  or or_1 (or_1_out, Input_A[0], Input_A[1], Input_A[2], Input_A[3], Input_A[4], Input_A[5], Input_A[6], Input_A[7], Input_A[9], Input_A[10], Input_A[11], Input_A[12], Input_A[13], Input_A[14], Input_A[15], Input_A[8]);

  assign Carry = CarryBorrow;
endmodule
